// Logisim project Prelab5Task3.circ as structural Verilog: 1 circuit, main circuit main
module main (
);

  wire Function_Generator, Oscilloscope, sn74hc541n_1_p7;

  // SN74HC541N sn74hc541n_1: pin names not known; wires that end beside it: 1'b0, Oscilloscope, Function_Generator, 1'b0, 1'b1, 1'b0, sn74hc541n_1_p7, sn74hc541n_1_p7, sn74hc541n_1_p7, sn74hc541n_1_p7
  Pull_Resistor pull_resistor_1 (.node(sn74hc541n_1_p7));
  // Discovery_P2_Connector discovery_p2_connector_1: pin names not known
endmodule
