// Logisim project homework4schematic.circ as structural Verilog: 1 circuit, main circuit main
module main (
);

  wire INPUT, sn74hc540n_1_p1, sn74hc540n_1_p4, sn74hc540n_1_p8, sn74hc540n_2_p1;

  // Discovery_P1_Connector discovery_p1_connector_1: pin names not known
  // SN74HC540N sn74hc540n_1: pin names not known; wires that end beside it: sn74hc540n_1_p1, 1'b0, sn74hc540n_1_p1, sn74hc540n_1_p4, 1'b0, 1'b1, 1'b0, sn74hc540n_1_p8, sn74hc540n_1_p8
  Pull_Resistor #(.pull(1)) pull_resistor_1 (.node(sn74hc540n_1_p8));
  // BarGraph_LED bargraph_led_1: pin names not known; wires that end beside it: sn74hc540n_1_p8, sn74hc540n_1_p8, 1'b0, 1'b0, 1'b0, 1'b0, 1'b0, 1'b0, 1'b0, 1'b0, 1'b0, 1'b0
  // Discovery_P2_Connector discovery_p2_connector_1: pin names not known
  // SN74HC540N sn74hc540n_2: pin names not known; wires that end beside it: sn74hc540n_2_p1, 1'b0, sn74hc540n_2_p1, 1'b0, 1'b1, 1'b0, INPUT

  // Notes on the sheet:
  //   LED0
  //   LED1
endmodule
