// Logisim project Prelab8Circ.circ as structural Verilog: 1 circuit, main circuit main
module main (
);

  wire lcd_2x16_1_p1, lcd_2x16_1_p2, lcd_2x16_1_p3, lcd_2x16_1_p4, lcd_2x16_1_p5, lcd_2x16_1_p6,
       lcd_2x16_1_p7, lcd_2x16_1_p8, lcd_2x16_1_p9, lm35_analog_temp_sensor_1_p2, sn74hc541n_1_p1,
       sn74hc541n_1_p2, sn74hc541n_1_p12, sn74hc541n_1_p13, sn74hc541n_1_p14, sn74hc541n_2_p12,
       sn74hc541n_2_p13, sn74hc541n_2_p14, sn74hc541n_2_p15, sn74hc541n_2_p16, sn74hc541n_2_p17,
       sn74hc541n_2_p18, sn74hc541n_2_p19;

  // LCD_2x16 lcd_2x16_1: pin names not known; wires that end beside it: lcd_2x16_1_p1, lcd_2x16_1_p2, lcd_2x16_1_p3, lcd_2x16_1_p4, lcd_2x16_1_p5, lcd_2x16_1_p6, lcd_2x16_1_p7, lcd_2x16_1_p8, lcd_2x16_1_p9
  // LM35_Analog_Temp_Sensor lm35_analog_temp_sensor_1: pin names not known; wires that end beside it: 1'b1, lm35_analog_temp_sensor_1_p2
  // OpAmp_741 opamp_741_1: pin names not known; wires that end beside it: 1'b0, lm35_analog_temp_sensor_1_p2, 1'b0, 1'b1, 1'b1, 1'b0
  // SN74HC541N sn74hc541n_1: pin names not known; wires that end beside it: sn74hc541n_1_p1, sn74hc541n_1_p2, 1'b1, 1'b1, 1'b0, sn74hc541n_1_p2, sn74hc541n_1_p1, lcd_2x16_1_p9, 1'b0, 1'b1, 1'b0, sn74hc541n_1_p12, sn74hc541n_1_p13, sn74hc541n_1_p14, 1'b0
  // SN74HC541N sn74hc541n_2: pin names not known; wires that end beside it: lcd_2x16_1_p8, lcd_2x16_1_p7, lcd_2x16_1_p6, lcd_2x16_1_p5, lcd_2x16_1_p4, lcd_2x16_1_p3, lcd_2x16_1_p2, lcd_2x16_1_p1, 1'b0, 1'b1, 1'b0, sn74hc541n_2_p12, sn74hc541n_2_p13, sn74hc541n_2_p14, sn74hc541n_2_p15, sn74hc541n_2_p16, sn74hc541n_2_p17, sn74hc541n_2_p18, sn74hc541n_2_p19, 1'b0, sn74hc541n_2_p13, sn74hc541n_2_p15, sn74hc541n_2_p17, sn74hc541n_2_p19, 1'b0, sn74hc541n_2_p12, sn74hc541n_2_p14, sn74hc541n_2_p16, sn74hc541n_2_p18
  // Discovery_P2_Connector discovery_p2_connector_1: pin names not known; wires that end beside it: 1'b0

  // Notes on the sheet:
  //   3.3V
  //   330 Ohm Resistor
  //   5V
  //   3.3V
  //   3.3V
  //   10k Resistor
  //   -3.3V
  //   3.3V
endmodule
