// Logisim project Prelab3Task2.circ as structural Verilog: 1 circuit, main circuit main
module main (
);

  wire PD0, PD1, PD2, PD3, PD4, PD5, PD6, PD7, PE8, Signal_Generator, sn74hc540n_1_p13;

  // SN74HC540N sn74hc540n_1: pin names not known; wires that end beside it: 1'b0, PD0, PD1, PD2, PD3, PD4, PD5, PD6, PD7, 1'b0, 1'b1, 1'b0, sn74hc540n_1_p13, sn74hc540n_1_p13, sn74hc540n_1_p13, sn74hc540n_1_p13, sn74hc540n_1_p13, sn74hc540n_1_p13, sn74hc540n_1_p13, sn74hc540n_1_p13
  Pull_Resistor pull_resistor_1 (.node(Signal_Generator));
  // SN74HC541N sn74hc541n_1: pin names not known; wires that end beside it: 1'b0, PE8, 1'b0, 1'b1, 1'b0, Signal_Generator
  Pull_Resistor #(.pull(1)) pull_resistor_2 (.node(sn74hc540n_1_p13));
  // BarGraph_LED bargraph_led_1: pin names not known; wires that end beside it: sn74hc540n_1_p13, sn74hc540n_1_p13, sn74hc540n_1_p13, sn74hc540n_1_p13, sn74hc540n_1_p13, sn74hc540n_1_p13, sn74hc540n_1_p13, sn74hc540n_1_p13, 1'b0, 1'b0, 1'b0, 1'b0, 1'b0, 1'b0, 1'b0, 1'b0, 1'b0, 1'b0
endmodule
