// Logisim project Prelab9Task3_schematic.circ as structural Verilog: 1 circuit, main circuit main
module main (
);

  wire dip_switch_1_p2, discovery_p1_connector_1_p1, discovery_p1_connector_1_p2,
       discovery_p1_connector_1_p3, discovery_p1_connector_1_p4, discovery_p2_connector_1_p2, LCD_E, LCD_R_W,
       LCD_RS_Pin, LCD_RST_pin, sn74hc540n_1_p3;

  // Discovery_P1_Connector discovery_p1_connector_1: pin names not known; wires that end beside it: discovery_p1_connector_1_p1, discovery_p1_connector_1_p2, discovery_p1_connector_1_p3, discovery_p1_connector_1_p4
  // HC_SR04_Ultrasonic_Sensor hc_sr04_ultrasonic_sensor_1: pin names not known; wires that end beside it: 1'b1
  // SN74HC541N sn74hc541n_1: pin names not known; wires that end beside it: 1'b0, discovery_p1_connector_1_p1, discovery_p1_connector_1_p2, discovery_p1_connector_1_p3, discovery_p1_connector_1_p4, 1'b0, 1'b1, 1'b0, LCD_R_W, LCD_E, LCD_RST_pin, LCD_RS_Pin
  // DIP_Switch dip_switch_1: pin names not known; wires that end beside it: 1'b0, dip_switch_1_p2, 1'b0, dip_switch_1_p2, 1'b0
  // SN74HC540N sn74hc540n_1: pin names not known; wires that end beside it: 1'b1, 1'b0, sn74hc540n_1_p3
  // Discovery_P2_Connector discovery_p2_connector_1: pin names not known; wires that end beside it: sn74hc540n_1_p3, discovery_p2_connector_1_p2

  // Notes on the sheet:
  //   VDD = +4.2V
endmodule
