// Logisim project homework5circuit.circ as structural Verilog: 1 circuit, main circuit main
module main (
);

  wire F, P1, P2, SA, SD1, SD2, sn74hc541n_1_p1, sn74hc541n_1_p3, sn74hc541n_1_p4, sn74hc541n_1_p5,
       sn74hc541n_1_p6, sn74hc541n_1_p7;

  // Discovery_P1_Connector discovery_p1_connector_1: pin names not known
  // SN74HC541N sn74hc541n_1: pin names not known; wires that end beside it: sn74hc541n_1_p1, 1'b0, sn74hc541n_1_p3, sn74hc541n_1_p4, sn74hc541n_1_p5, sn74hc541n_1_p6, sn74hc541n_1_p7, sn74hc541n_1_p1, 1'b0, 1'b1, 1'b0, SA, F, P1, P2, SD1, SD2
  // Discovery_P2_Connector discovery_p2_connector_1: pin names not known; wires that end beside it: sn74hc541n_1_p3
endmodule
