// Logisim project prelab11_circ.circ as structural Verilog: 1 circuit, main circuit main
module main (
);

  wire capacitor_1_p2, capacitor_1_p5, discovery_p1_connector_1_p1, pull_resistor_3_node, sn74hc541n_1_p6;

  // Discovery_P1_Connector discovery_p1_connector_1: pin names not known; wires that end beside it: discovery_p1_connector_1_p1
  // SN74HC541N sn74hc541n_1: pin names not known; wires that end beside it: 1'b0, discovery_p1_connector_1_p1, 1'b0, 1'b1, 1'b0, sn74hc541n_1_p6
  // Diode diode_1: pin names not known; wires that end beside it: 1'b1, sn74hc541n_1_p6, 1'b1
  Pull_Resistor pull_resistor_1 (.node(sn74hc541n_1_p6));
  // Capacitor capacitor_1: pin names not known; wires that end beside it: sn74hc541n_1_p6, capacitor_1_p2, capacitor_1_p2, 1'b0, capacitor_1_p5
  Pull_Resistor #(.pull(1)) pull_resistor_2 (.node(capacitor_1_p5));
  Pull_Resistor #(.pull(1)) pull_resistor_3 (.node(pull_resistor_3_node));
  // Relay_DPDT relay_dpdt_1: pin names not known; wires that end beside it: pull_resistor_3_node
  // also tied to GND on the sheet: {sn74hc541n_1_p6, capacitor_1_p5}
  // also tied to VCC on the sheet: pull_resistor_3_node

  // Notes on the sheet:
  //   Free-wheeling diode
  //   1kOhm
  //   2n3904
  //   10uF
  //   2.2Kohm
  //   12kOhm
endmodule
