// Logisim project prelab10 task1 schematic.circ as structural Verilog: 1 circuit, main circuit main
module main (
);

  wire discovery_p1_connector_1_p1, discovery_p1_connector_1_p2, discovery_p1_connector_1_p3,
       discovery_p1_connector_1_p4, discovery_p1_connector_1_p5, discovery_p1_connector_1_p6, sram_1_p3,
       sram_1_p4, sram_1_p11, sram_1_p13, sram_1_p15, sram_1_p16, sram_1_p18, sram_1_p20, sram_1_p21,
       sram_1_p22;

  // Discovery_P1_Connector discovery_p1_connector_1: pin names not known; wires that end beside it: discovery_p1_connector_1_p1, discovery_p1_connector_1_p2, discovery_p1_connector_1_p3, discovery_p1_connector_1_p4, discovery_p1_connector_1_p5, discovery_p1_connector_1_p6
  // SRAM sram_1: pin names not known; wires that end beside it: 1'b0, 1'b0, sram_1_p3, sram_1_p4, discovery_p1_connector_1_p4, discovery_p1_connector_1_p1, discovery_p1_connector_1_p5, discovery_p1_connector_1_p2, discovery_p1_connector_1_p6, discovery_p1_connector_1_p3, sram_1_p11, 1'b1, sram_1_p13, 1'b0, sram_1_p15, sram_1_p16, 1'b0, sram_1_p18, 1'b0, sram_1_p20, sram_1_p21, sram_1_p22
  // Discovery_P2_Connector discovery_p2_connector_1: pin names not known
endmodule
